# Fritzing sketch ESP8266_FTDI_RST (saved by Fritzing 0.9.0b)

parts:
  U1 = ESP8266 WiFi Module [part_number=ESP8266]
  U3 = V_REG_LD1117VXX [package=78xxl]
  Part1 = FTDI Basic Programmer
  S1 = Pushbutton [package="[THT]"]
  S2 = Pushbutton [package="[THT]"]
  R1 = Resistor [tolerance=±5% resistance=10k package=THT]

nets:
  N1: U1.RXD, Part1.TXO
  N2: U1.VCC, U1.CH_PD, U3.OUT
  GND: U1.GPIO_0, U1.GND, U3.GND, Part1.GND, S1.Pin_1, S1.Pin_2
  N3: U1.GPIO_16, S2.Pin_2, R1.Pin_0
  N4: U1.TXD, Part1.RXI
  N5: U3.IN, Part1.POWER

custom parts:
  ESP8266 WiFi Module: Generic WiFi Module based on the ESP8266 with onboard PCB antenna and UART communications
